# Fritzing sketch buttons (saved by Fritzing 0.9.2b)
breadboards: 1

parts:
  Q1 = PNP-Transistor [package="TO92 [THT]"]
  R1 = Resistor [tolerance=±5% resistance=220 package=THT]
  R2 = Resistor [tolerance=±5% resistance=220 package=THT]
  R3 = Resistor [tolerance=±5% resistance=220 package=THT]
  LED1 = LED - 5mm [color="Red (633nm)" package="5 mm [THT]"]
  S2 = Pushbutton [package="[THT]"]
  LED2 = LED - 5mm [color="Red (633nm)" package="5 mm [THT]"]
  R4 = Resistor [tolerance=±5% resistance=220 package=THT]
  S3 = Pushbutton [package="[THT]"]
  R5 = Resistor [tolerance=±5% resistance=220 package=THT]
  J1 = female pin header, 2 pins [form="♀ (female)"]
  J2 = male pin header, 2 pins [form="♂ (male)"]
  J3 = female pin header, 2 pins [form="♀ (female)"]
  J4 = male pin header, 2 pins [form="♂ (male)"]

nets:
  5V: Q1.E
  N1: Q1.B, R1.Pin_1
  D4: Q1.C, J2.pin1
  D3: R1.Pin_0, J4.pin2
  N2: R2.Pin_0, R3.Pin_1, LED1.anode
  N3: R2.Pin_1, S2.Pin_3, S2.Pin_4
  N4: R3.Pin_0, J1.pin1
  N5: LED1.cathode, S2.Pin_1, S2.Pin_2, J1.pin2
  N6: LED2.cathode, R4.Pin_0, R5.Pin_1
  N7: LED2.anode, S3.Pin_1, S3.Pin_2, J3.pin2
  N8: R4.Pin_1, S3.Pin_3, S3.Pin_4
  N9: R5.Pin_0, J3.pin1
  D2: J2.pin2, J4.pin1

notes:
  simple version
  version with transistor
