# Fritzing sketch quizz (saved by Fritzing 0.9.2b)
breadboards: 1

parts:
  Part1 = Arduino Uno (Rev3)
  LED1 = LED - 5mm [color="Red (633nm)" package="5 mm [THT]"]
  LED2 = LED - 5mm [color="Red (633nm)" package="5 mm [THT]"]
  LED3 = LED - 5mm [color="Red (633nm)" package="5 mm [THT]"]
  LED4 = LED - 5mm [color="Red (633nm)" package="5 mm [THT]"]
  LED0 = LED - 5mm [color="Red (633nm)" package="5 mm [THT]"]
  R1 = Resistor [tolerance=±5% resistance=220 package=THT]
  S1 = Pushbutton [package="[THT]"]
  S2 = Pushbutton [package="[THT]"]
  S3 = Pushbutton [package="[THT]"]
  S4 = Pushbutton [package="[THT]"]
  S0 = Pushbutton [package="[THT]"]
  SPKR1 = Loudspeaker

nets:
  N1: Part1.A0, S0.Pin_1, S0.Pin_2
  N2: Part1.A1, S1.Pin_1, S1.Pin_2
  N3: Part1.A2, S2.Pin_1, S2.Pin_2
  N4: Part1.A3, S3.Pin_1, S3.Pin_2
  N5: Part1.A4/SDA, S4.Pin_1, S4.Pin_2
  N6: Part1.D8, LED0.anode
  N7: Part1.D9_PWM, LED1.anode
  N8: Part1.D10_PWM/SS, LED2.anode
  N9: Part1.D11_PWM/MOSI, LED3.anode
  N10: Part1.D12/MISO, LED4.anode
  GND: Part1.GND, R1.Pin_1, S1.Pin_3, S1.Pin_4, S2.Pin_3, S2.Pin_4, S3.Pin_3, S3.Pin_4, S4.Pin_3, S4.Pin_4, S0.Pin_3, S0.Pin_4, SPKR1.pin1
  N11: LED1.cathode, LED2.cathode, LED3.cathode, LED4.cathode, LED0.cathode, R1.Pin_0
