# Fritzing sketch montage (saved by Fritzing 0.9.6b)
circuit board: 5.65068cm x 5.24508cm
breadboards: 1

parts:
  R1 = Resistor [tolerance=±5% power=0.25 resistance=220 package=THT]
  LED1 = LED - 5mm [color="Green (570nm)" current=0.030 package="5 mm [THT]"]
  S1 = Pushbutton [package="[THT]"]
  S2 = Pushbutton [package="[THT]"]
  S3 = Pushbutton [package="[THT]"]
  S4 = Pushbutton [package="[THT]"]
  R2 = Resistor [tolerance=±5% power=0.25 resistance=220 package=THT]
  R3 = Resistor [tolerance=±5% power=0.25 resistance=220 package=THT]
  R4 = Resistor [tolerance=±5% power=0.25 resistance=220 package=THT]
  LED2 = LED - 5mm [color="Yellow (592nm)" current=0.030 package="5 mm [THT]"]
  LED3 = LED - 5mm [color="Red (633nm)" current=0.030 package="5 mm [THT]"]
  LED4 = LED - 5mm [color="White (6500K)" current=0.030 package="5 mm [THT]"]
  Part1 = Arduino Uno (Rev3)

nets:
  N1: R1.Pin_0, S1.Pin_3, S1.Pin_4, S2.Pin_3, S2.Pin_4, S3.Pin_1, S3.Pin_2, S4.Pin_1, S4.Pin_2, R2.Pin_0, R3.Pin_1, R4.Pin_1
  N2: R1.Pin_1, LED1.cathode
  6: LED1.anode, Part1.D6_PWM
  11: S1.Pin_1, S1.Pin_2, Part1.D11_PWM/MOSI
  10: S2.Pin_1, S2.Pin_2, Part1.D10_PWM/SS
  8: S3.Pin_3, S3.Pin_4, Part1.D8
  9: S4.Pin_3, S4.Pin_4, Part1.D9_PWM
  N3: R2.Pin_1, LED2.cathode
  N4: R3.Pin_0, LED3.cathode
  N5: R4.Pin_0, LED4.cathode
  5: LED2.anode, Part1.D5_PWM
  3: LED3.anode, Part1.D3_PWM
  4: LED4.anode, Part1.D4
